# Fritzing sketch Smartbin (saved by Fritzing 0.8.7b)
breadboards: 2

parts:
  LC_Amp_1 = HX711 Weighing Sensor Module
  LC_Amp_2 = HX711 Weighing Sensor Module
  LC_Amp_3 = HX711 Weighing Sensor Module
  LC_Amp_4 = HX711 Weighing Sensor Module
  TCS34725_RGB_Sensor = Adafruit TCS34725 RGB Color Sensor [part_number="Adafruit #1334"]
  Load_Cell_4 = Load Cell - Red/white/black/green
  Load_Cell_3 = Load Cell - Red/white/black/green
  Load_Cell_2 = Load Cell - Red/white/black/green
  Load_Cell_1 = Load Cell - Red/white/black/green
  Part5 = Arduino Uno (Rev3)
  Servo_2 = Basic Servo
  Servo_3 = Basic Servo
  Servo_4 = Basic Servo
  Servo_1 = Basic Servo

nets:
  VCC: LC_Amp_1.VCC, LC_Amp_2.VCC, LC_Amp_3.VCC, LC_Amp_4.VCC, TCS34725_RGB_Sensor.VIN, Part5.5V, Servo_2.vcc, Servo_3.vcc, Servo_4.vcc, Servo_1.vcc
  GND: LC_Amp_1.GND, LC_Amp_2.GND, LC_Amp_3.GND, LC_Amp_4.GND, TCS34725_RGB_Sensor.GND, Part5.GND, Servo_2.gnd, Servo_3.gnd, Servo_4.gnd, Servo_1.gnd
  N1: LC_Amp_1.DO/RX, Part5.D3_PWM
  N2: LC_Amp_1.CK/TX, Part5.D2
  N3: LC_Amp_1.E+, Load_Cell_1.wire1
  N4: LC_Amp_1.E-, Load_Cell_1.wire3
  N5: LC_Amp_1.A+, Load_Cell_1.wire4
  N6: LC_Amp_1.A-, Load_Cell_1.wire2
  N7: LC_Amp_2.DO/RX, Part5.D5_PWM
  N8: LC_Amp_2.CK/TX, Part5.D4
  N9: LC_Amp_2.E+, Load_Cell_2.wire1
  N10: LC_Amp_2.E-, Load_Cell_2.wire3
  N11: LC_Amp_2.A+, Load_Cell_2.wire4
  N12: LC_Amp_2.A-, Load_Cell_2.wire2
  N13: LC_Amp_3.DO/RX, Part5.D7
  N14: LC_Amp_3.CK/TX, Part5.D6_PWM
  N15: LC_Amp_3.E+, Load_Cell_3.wire1
  N16: LC_Amp_3.E-, Load_Cell_3.wire3
  N17: LC_Amp_3.A+, Load_Cell_3.wire4
  N18: LC_Amp_3.A-, Load_Cell_3.wire2
  N19: LC_Amp_4.DO/RX, Part5.D9_PWM
  N20: LC_Amp_4.CK/TX, Part5.D8
  N21: LC_Amp_4.E+, Load_Cell_4.wire1
  N22: LC_Amp_4.E-, Load_Cell_4.wire3
  N23: LC_Amp_4.A+, Load_Cell_4.wire4
  N24: LC_Amp_4.A-, Load_Cell_4.wire2
  N25: TCS34725_RGB_Sensor.SCL, Part5.A5/SCL
  N26: TCS34725_RGB_Sensor.SDA, Part5.A4/SDA
  N27: Part5.A0, Servo_1.pulse
  N28: Part5.A1, Servo_2.pulse
  N29: Part5.A2, Servo_3.pulse
  N30: Part5.A3, Servo_4.pulse

custom parts:
  Adafruit TCS34725 RGB Color Sensor: Your electronics can now see in dazzling color with this lovely color light sensor. We found the best color sensor on the market, the TCS34725, which has RGB and Clear light sensing elements. An IR blocking filter, integrated on-chip and localized to the color sensing photodiodes, minimizes the IR spectral component of the incoming light and allows color measurements to be made accurately. The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
  Load Cell - Red/white/black/green: A rectangle load cell/weighting pressure Sensor with four wires - Red, white, black, green. Normally corresponding with E+, E-, A+, A- respectively.
